// Logisim project nand2tetris.circ as structural Verilog: 7 circuits, main circuit main
module main (
  input  in_1,
  input  in_2,
  input  in_3,
  input  in_4,
  input  in_5,
  input  in_6,
  input  in_7,
  input  in_8,
  input  in_9,
  input  in_10,
  input  in_11,
  input  in_12,
  output out_13,
  output out_14,
  output out_15,
  output out_16,
  output out_17,
  output out_18,
  output out_19
);

  Mux mux_1 (.a(in_2), .b(in_3), .sel(in_5), .outp(out_14));
  DMux dmux_1 (.in_1(in_9), .in_2(in_11), .out_3(out_17), .out_4(out_18));
  AndGate andgate_1 (.a(in_4), .b(in_6), .outp(out_15));
  NotGate notgate_1 (.inp(in_1), .outp(out_13));
  OrGate orgate_1 (.a(in_8), .b(in_7), .outp(out_16));
  XorGate xorgate_1 (.in_1(in_12), .in_2(in_10), .out_3(out_19));
endmodule

module NotGate (
  input  inp,
  output outp
);

  nand nand_1 (outp, inp, inp);
endmodule

module AndGate (
  input  a,
  input  b,
  output outp
);

  wire nand_1_out;

  nand nand_1 (nand_1_out, a, b);
  NotGate notgate_1 (.inp(nand_1_out), .outp(outp));
endmodule

module OrGate (
  input  a,
  input  b,
  output outp
);

  wire notgate_1_outp, notgate_2_outp;

  NotGate notgate_1 (.inp(a), .outp(notgate_1_outp));
  NotGate notgate_2 (.inp(b), .outp(notgate_2_outp));
  nand nand_1 (outp, notgate_1_outp, notgate_2_outp);
endmodule

module XorGate (
  input  in_1,
  input  in_2,
  output out_3
);

  wire nand_1_out, orgate_1_outp;

  nand nand_1 (nand_1_out, in_1, in_2);
  OrGate orgate_1 (.a(in_2), .b(in_1), .outp(orgate_1_outp));
  AndGate andgate_1 (.a(nand_1_out), .b(orgate_1_outp), .outp(out_3));
endmodule

module Mux (
  input  a,
  input  b,
  input  sel,
  output outp
);

  wire andgate_1_outp, andgate_2_outp, notgate_1_outp;

  NotGate notgate_1 (.inp(sel), .outp(notgate_1_outp));
  AndGate andgate_1 (.a(notgate_1_outp), .b(a), .outp(andgate_1_outp));
  AndGate andgate_2 (.a(b), .b(sel), .outp(andgate_2_outp));
  OrGate orgate_1 (.a(andgate_2_outp), .b(andgate_1_outp), .outp(outp));
endmodule

module DMux (
  input  in_1,
  input  in_2,
  output out_3,
  output out_4
);

  wire notgate_1_outp;

  NotGate notgate_1 (.inp(in_2), .outp(notgate_1_outp));
  AndGate andgate_1 (.a(notgate_1_outp), .b(in_1), .outp(out_3));
  AndGate andgate_2 (.a(in_1), .b(in_2), .outp(out_4));
endmodule
